# Fritzing sketch treadmill (saved by Fritzing 0.9.3b)
circuit board: 7.23178cm x 3.07559cm

parts:
  treadmill_header = Header 8 [package=bm08b-srss-tb]
  3_3V_to_5V = Logic Level Converter
  DC-DC_step-down = LM2596 step down module
  pi_power = Header 2 [package=jst-2-pth-ns]
  Raspberry_Pi_Zero1 = Raspberry Pi Zero

nets:
  N1: treadmill_header.1, DC-DC_step-down.IN-, DC-DC_step-down.OUT-, pi_power.1
  N2: treadmill_header.2, DC-DC_step-down.IN+
  N3: treadmill_header.4, 3_3V_to_5V.TX2_HV
  N4: treadmill_header.5, Raspberry_Pi_Zero1.GPIO20
  N5: treadmill_header.6, Raspberry_Pi_Zero1.GPIO21
  N6: 3_3V_to_5V.TX2_LV, Raspberry_Pi_Zero1.GPIO18
  GND: 3_3V_to_5V.GND, Raspberry_Pi_Zero1.GND
  3V3: 3_3V_to_5V.LV, Raspberry_Pi_Zero1.3v3, Raspberry_Pi_Zero1.3V3
  N7: 3_3V_to_5V.HV, Raspberry_Pi_Zero1.5V
  N8: DC-DC_step-down.OUT+, pi_power.2

notes:
  1 - Black, ground
  2 - Red, +13 VDC
  3 - Green, Speed sensor, 0-5 VDC
  4 - Blue, PWM signal to set speed
  5 - Orange, Incline up
  6 - Yellow, Incline down
  7 - Violet, Incline sensor
  8 - Black, ground
  (MC5100DTS)
  1 - Black, ground
  2 - Red, +5 VDC
  Power for Pi Zero

custom parts:
  LM2596 step down module: LM2596 DC-DC step down power supply module 3 A.
